// Logisim project LAB_5_TANVIR_SADAT.circ as structural Verilog: 4 circuits, main circuit main
module main (
  input  in_1,
  input  [3:0] in_2,
  output [11:0] out_3,
  output out_4
);

  wire clock_1_out;
  wire [11:0] n12_bit_register_file_1_out_7, n12_bit_register_file_1_out_8, rom_1_data;

  ROM #(.addrWidth(4), .dataWidth(12)) rom_1 (.addr(in_2), .data(rom_1_data));  // open: sel
  Clock clock_1 (.out(clock_1_out));
  _12_bit_register_file u_12_bit_register_file_1 (
    .in_2(out_3), .in_4(rom_1_data[2:0]), .in_5(rom_1_data[11]), .out_7(n12_bit_register_file_1_out_7),
    .in_1(rom_1_data[5:3]), .out_8(n12_bit_register_file_1_out_8), .in_3(rom_1_data[8:6]), .clock(clock_1_out));
  _12_bit_alu u_12_bit_alu_1 (
    .in_1(in_1), .in_2(n12_bit_register_file_1_out_7), .in_3(n12_bit_register_file_1_out_8),
    .in_4(rom_1_data[10:9]), .out_5(out_3), .out_6(out_4));

  // Notes on the sheet:
  //   contents of rom_1 (hex, n*v repeats v):
  //   c50 e0a
endmodule

module _12_bit_register_file (
  input  [2:0] in_1,
  input  [11:0] in_2,
  input  [2:0] in_3,
  input  [2:0] in_4,
  input  in_5,
  input  clock,
  output [11:0] out_7,
  output [11:0] out_8
);

  wire and_1_out, decoder_1_out0, decoder_1_out1, decoder_1_out2, decoder_1_out3, decoder_1_out4,
       decoder_1_out5, decoder_1_out6, decoder_1_out7;
  wire [11:0] demultiplexer_1_out0, demultiplexer_1_out1, demultiplexer_1_out2, demultiplexer_1_out3,
       demultiplexer_1_out4, demultiplexer_1_out5, demultiplexer_1_out6, demultiplexer_1_out7, register_1_q,
       register_2_q, register_3_q, register_4_q, register_5_q, register_6_q, register_7_q, register_8_q;

  Demultiplexer #(.select(3), .width(12)) demultiplexer_1 (
    .out0(demultiplexer_1_out0), .out1(demultiplexer_1_out1), .out2(demultiplexer_1_out2),
    .out3(demultiplexer_1_out3), .out4(demultiplexer_1_out4), .out5(demultiplexer_1_out5),
    .out6(demultiplexer_1_out6), .out7(demultiplexer_1_out7), .in(in_2), .sel(in_4));  // open: en
  Decoder #(.select(3)) decoder_1 (
    .out0(decoder_1_out0), .out1(decoder_1_out1), .out2(decoder_1_out2), .out3(decoder_1_out3),
    .out4(decoder_1_out4), .out5(decoder_1_out5), .out6(decoder_1_out6), .out7(decoder_1_out7), .sel(in_4));  // open: en
  and and_1 (and_1_out, in_5, clock);
  Register #(.width(12)) register_1 (
    .D(demultiplexer_1_out0), .en(decoder_1_out0), .Q(register_1_q), .clk(and_1_out));  // open: clr
  Register #(.width(12)) register_2 (
    .D(demultiplexer_1_out1), .en(decoder_1_out1), .Q(register_2_q), .clk(and_1_out));  // open: clr
  Register #(.width(12)) register_3 (
    .D(demultiplexer_1_out2), .en(decoder_1_out2), .Q(register_3_q), .clk(and_1_out));  // open: clr
  Register #(.width(12)) register_4 (
    .D(demultiplexer_1_out3), .en(decoder_1_out3), .Q(register_4_q), .clk(and_1_out));  // open: clr
  Register #(.width(12)) register_5 (
    .D(demultiplexer_1_out4), .en(decoder_1_out4), .Q(register_5_q), .clk(and_1_out));  // open: clr
  Register #(.width(12)) register_6 (
    .D(demultiplexer_1_out5), .en(decoder_1_out5), .Q(register_6_q), .clk(and_1_out));  // open: clr
  Register #(.width(12)) register_7 (
    .D(demultiplexer_1_out6), .en(decoder_1_out6), .Q(register_7_q), .clk(and_1_out));  // open: clr
  Register #(.width(12)) register_8 (
    .D(demultiplexer_1_out7), .en(decoder_1_out7), .Q(register_8_q), .clk(and_1_out));  // open: clr
  Multiplexer #(.select(3), .width(12)) multiplexer_1 (
    .in0(register_1_q), .in1(register_2_q), .in2(register_3_q), .in3(register_4_q), .in4(register_5_q),
    .in5(register_6_q), .in6(register_7_q), .in7(register_8_q), .out(out_7), .sel(in_1));  // open: en
  Multiplexer #(.select(3), .width(12)) multiplexer_2 (
    .in0(register_1_q), .in1(register_2_q), .in2(register_3_q), .in3(register_4_q), .in4(register_5_q),
    .in5(register_6_q), .in6(register_7_q), .in7(register_8_q), .out(out_8), .sel(in_3));  // open: en
endmodule

module ALU_DESIGN (
  input  Cin,
  input  A,
  input  [1:0] in_3,
  input  B,
  output \output ,
  output Cout
);

  wire adder_1_cout, adder_1_out, and_1_out, or_1_out, subtractor_1_bout, subtractor_1_out;

  and and_1 (and_1_out, A, B);
  or or_1 (or_1_out, A, B);
  Adder #(.width(1)) adder_1 (.a(A), .b(B), .out(adder_1_out), .cin(Cin), .cout(adder_1_cout));
  Subtractor #(.width(1)) subtractor_1 (.a(A), .b(B), .out(subtractor_1_out), .bin(Cin), .bout(subtractor_1_bout));
  Multiplexer multiplexer_1 (.in0(adder_1_cout), .in1(subtractor_1_bout), .out(Cout), .sel(in_3[0]), .en(in_3[1]));
  Multiplexer #(.select(2)) multiplexer_2 (
    .in0(and_1_out), .in1(or_1_out), .in2(adder_1_out), .in3(subtractor_1_out), .out(\output ), .sel(in_3));  // open: en

  // Notes on the sheet:
  //   Opcode
endmodule

module _12_bit_alu (
  input  in_1,
  input  [11:0] in_2,
  input  [11:0] in_3,
  input  [1:0] in_4,
  output [11:0] out_5,
  output out_6
);

  wire alu_design_1_cout, alu_design_2_cout, alu_design_3_cout, alu_design_4_cout, alu_design_5_cout,
       alu_design_6_cout, alu_design_8_cout, alu_design_9_cout, alu_design_10_cout, alu_design_11_cout;

  ALU_DESIGN alu_design_1 (
    .Cin(alu_design_6_cout), .A(in_2[5]), .B(in_3[5]), .\output (out_5[5]), .in_3(in_4),
    .Cout(alu_design_1_cout));
  ALU_DESIGN alu_design_2 (
    .Cin(in_1), .A(in_2[0]), .B(in_3[0]), .\output (out_5[0]), .in_3(in_4), .Cout(alu_design_2_cout));
  ALU_DESIGN alu_design_3 (
    .Cin(alu_design_2_cout), .A(in_2[1]), .B(in_3[1]), .\output (out_5[1]), .in_3(in_4),
    .Cout(alu_design_3_cout));
  ALU_DESIGN alu_design_4 (
    .Cin(alu_design_3_cout), .A(in_2[2]), .B(in_3[2]), .\output (out_5[2]), .in_3(in_4),
    .Cout(alu_design_4_cout));
  ALU_DESIGN alu_design_5 (
    .Cin(alu_design_4_cout), .A(in_2[3]), .B(in_3[3]), .\output (out_5[3]), .in_3(in_4),
    .Cout(alu_design_5_cout));
  ALU_DESIGN alu_design_6 (
    .Cin(alu_design_5_cout), .A(in_2[4]), .B(in_3[4]), .\output (out_5[4]), .in_3(in_4),
    .Cout(alu_design_6_cout));
  ALU_DESIGN alu_design_7 (
    .Cin(alu_design_1_cout), .A(in_2[6]), .B(in_3[6]), .\output (out_5[6]), .in_3(in_4), .Cout(in_2[9]));
  ALU_DESIGN alu_design_8 (
    .Cin(in_2[9]), .A(in_2[7]), .B(in_3[7]), .\output (out_5[7]), .in_3(in_4), .Cout(alu_design_8_cout));
  ALU_DESIGN alu_design_9 (
    .Cin(alu_design_8_cout), .A(in_2[8]), .B(in_3[8]), .\output (out_5[8]), .in_3(in_4),
    .Cout(alu_design_9_cout));
  ALU_DESIGN alu_design_10 (
    .Cin(alu_design_9_cout), .A(in_2[9]), .B(in_3[9]), .\output (out_5[9]), .in_3(in_4),
    .Cout(alu_design_10_cout));
  ALU_DESIGN alu_design_11 (
    .Cin(alu_design_10_cout), .A(in_2[10]), .B(in_3[10]), .\output (out_5[10]), .in_3(in_4),
    .Cout(alu_design_11_cout));
  ALU_DESIGN alu_design_12 (
    .Cin(alu_design_11_cout), .A(in_2[11]), .B(in_3[11]), .\output (out_5[11]), .in_3(in_4), .Cout(out_6));

  // Notes on the sheet:
  //   0
  //   1
  //   2
  //   4
  //   5
  //   6
  //   3
  //   7
  //   8
  //   9
  //   10
  //   11
endmodule
